// Logisim project proj_2_2.circ as structural Verilog
module inst_fetch (
  input  clk,
  input  rst,
  input  control_en_i,
  input  [31:0] control_pc_i,
  input  [15:0] inst_i,
  output inst_en_o,
  output [31:0] current_pc_o,
  output [31:0] inst_addr_o,
  output [15:0] inst_o
);

  wire not_1_out, not_2_out;
  wire [31:0] adder_1_out, counter_1_q, multiplexer_1_out;

  not not_1 (not_1_out, rst);
  Adder #(.width(32)) adder_1 (.a(control_pc_i), .b(32'h1), .out(adder_1_out));  // open: cin, cout
  Counter #(.max('hffffffff), .width(32)) counter_1 (
    .clr(rst), .load(control_en_i), .up(not_1_out), .count(not_1_out), .clk(clk), .D(adder_1_out),
    .Q(counter_1_q));  // open: carry
  Multiplexer #(.width(32)) multiplexer_1 (
    .in0(counter_1_q), .in1(control_pc_i), .out(multiplexer_1_out), .sel(control_en_i));
  not not_2 (not_2_out, rst);
  Register #(.width(32)) register_1 (.D(multiplexer_1_out), .en(not_2_out), .clk(clk), .Q(current_pc_o), .clr(rst));
  not not_3 (inst_en_o, rst);

  assign inst_addr_o = current_pc_o;
  assign inst_o = inst_i;

  // Notes on the sheet:
  //   Don't touch
endmodule

module TOP (
  input  rst,
  input  clk,
  input  [15:0] inst,
  input  [31:0] mem_result,
  input  [31:0] current_pc,
  output mem_wen,
  output [31:0] mem_din,
  output mem_ren,
  output [31:0] alu_result,
  output control_en,
  output [31:0] control_pc,
  output wb_en,
  output [4:0] wb_addr,
  output [31:0] wb_data
);

  wire and_2_out, comparator_1_eq, comparator_2_eq, control_enable, halt, multiplexer_2_out,
       multiplexer_13_out, multiplexer_17_out, multiplexer_25_out, multiplexer_26_out, not_1_out, not_2_out,
       not_3_out, not_4_out, not_5_out, not_6_out, not_7_out, not_8_out, not_9_out, op2_src, re, reg_en,
       wb_src, we;
  wire [3:0] ALU_ctrl, CR_type, multiplexer_31_out, multiplexer_33_out;
  wire [4:0] adder_1_out, adder_2_out, adder_3_out, bit_extender_4_out, bit_extender_6_out,
       bit_extender_7_out, multiplexer_3_out, rd, rs1, rs2;
  wire [31:0] adder_4_out, adder_5_out, bit_extender_1_out, bit_extender_2_out, bit_extender_3_out,
       bit_extender_5_out, bit_extender_8_out, bit_extender_9_out, imm, multiplexer_9_out,
       multiplexer_10_out, multiplexer_11_out, multiplexer_12_out, multiplexer_15_out, multiplexer_18_out,
       multiplexer_20_out, multiplexer_24_out, multiplexer_32_out, pc_change, regfile_1_x_rs2, x_rs1;

  not not_1 (not_1_out, inst[0]);
  not not_2 (not_2_out, inst[1]);
  not not_3 (not_3_out, inst[13]);
  not not_4 (not_4_out, inst[14]);
  assign bit_extender_1_out = {{25{inst[5]}}, {inst[5], inst[12:10], inst[6], 2'b00}};  // Bit_Extender bit_extender_1
  assign bit_extender_2_out = {{26{inst[12]}}, {inst[12], inst[6:2]}};  // Bit_Extender bit_extender_2
  assign bit_extender_3_out = {{24{inst[8]}}, {inst[8:7], inst[12:9], 2'b00}};  // Bit_Extender bit_extender_3
  assign bit_extender_4_out = {{2{1'b0}}, inst[4:2]};  // Bit_Extender bit_extender_4
  Multiplexer #(.width(5)) multiplexer_1 (.in0(multiplexer_3_out), .in1({5{1'b0}}), .out(wb_addr), .sel(halt));
  and and_1 (halt, not_1_out, not_2_out, not_3_out, not_4_out, inst[15]);
  assign bit_extender_5_out = {{22{inst[10]}}, {inst[10:7], inst[12:11], inst[5], inst[6], 2'b00}};  // Bit_Extender bit_extender_5
  assign bit_extender_6_out = {{2{1'b0}}, inst[9:7]};  // Bit_Extender bit_extender_6
  assign bit_extender_7_out = {{2{1'b0}}, inst[4:2]};  // Bit_Extender bit_extender_7
  assign bit_extender_8_out = {{20{inst[12]}}, {inst[12], inst[8], inst[10:9], inst[6], inst[7], inst[2], inst[11], inst[5:3], 1'b0}};  // Bit_Extender bit_extender_8
  Adder #(.width(5)) adder_1 (.a(bit_extender_4_out), .b(5'b01000), .out(adder_1_out));  // open: cin, cout
  Adder #(.width(5)) adder_2 (.a(bit_extender_6_out), .b(5'b01000), .out(adder_2_out));  // open: cin, cout
  Adder #(.width(5)) adder_3 (.a(bit_extender_7_out), .b(5'b01000), .out(adder_3_out));  // open: cin, cout
  Multiplexer multiplexer_2 (.in0(reg_en), .in1(1'b0), .out(multiplexer_2_out), .sel(rst));
  Multiplexer #(.width(5)) multiplexer_3 (.in0(rd), .in1({5{1'b0}}), .out(multiplexer_3_out), .sel(rst));
  Multiplexer #(.select(4), .width(32)) multiplexer_4 (
    .in0(bit_extender_2_out), .in1(bit_extender_3_out), .in3(bit_extender_5_out), .in4(bit_extender_2_out),
    .in6(bit_extender_2_out), .in7(bit_extender_2_out), .in8(bit_extender_1_out), .in9(bit_extender_1_out),
    .in10(bit_extender_9_out), .in11(bit_extender_8_out), .out(imm), .sel(ALU_ctrl));  // open: in2, in5, in12, in13, in14, in15
  Multiplexer multiplexer_5 (.in0(multiplexer_2_out), .in1(1'b0), .out(wb_en), .sel(halt));
  Regfile regfile_1 (
    .rst(rst), .clk(clk), .x_rd(multiplexer_32_out), .wb_en(multiplexer_2_out), .rs1(rs1), .rd(rd),
    .rs2(rs2), .x_rs1(x_rs1), .x_rs2(regfile_1_x_rs2));
  Multiplexer #(.select(4), .width(5)) multiplexer_6 (
    .in0(inst[11:7]), .in1({5{1'b0}}), .in2(inst[11:7]), .in3(adder_1_out), .in4(inst[11:7]),
    .in5(inst[11:7]), .in6(inst[11:7]), .in7(inst[11:7]), .in8(adder_1_out), .in9({5{1'b0}}),
    .in10({5{1'b0}}), .in11({5{1'b0}}), .in12(inst[11:7]), .out(rd), .sel(ALU_ctrl));  // open: in13, in14, in15
  Multiplexer #(.select(4), .width(5)) multiplexer_7 (
    .in0(inst[11:7]), .in1(5'b00010), .in2({5{1'b0}}), .in3(5'b00010), .in4(inst[11:7]), .in5(inst[11:7]),
    .in6({5{1'b0}}), .in7({5{1'b0}}), .in8(adder_2_out), .in9(adder_2_out), .in10(adder_2_out),
    .in11({5{1'b0}}), .in12(inst[11:7]), .out(rs1), .sel(ALU_ctrl));  // open: in13, in14, in15
  Multiplexer #(.select(4), .width(5)) multiplexer_8 (
    .in1(inst[6:2]), .in2(inst[6:2]), .in3({5{1'b0}}), .in4({5{1'b0}}), .in5(inst[6:2]), .in6({5{1'b0}}),
    .in7({5{1'b0}}), .in8({5{1'b0}}), .in9(adder_3_out), .in10({5{1'b0}}), .in11({5{1'b0}}),
    .in12({5{1'b0}}), .out(rs2), .sel(ALU_ctrl));  // open: in0, in13, in14, in15
  assign bit_extender_9_out = {{23{inst[12]}}, {inst[12], inst[6:5], inst[2], inst[11:10], inst[4:3], 1'b0}};  // Bit_Extender bit_extender_9
  Adder #(.width(32)) adder_4 (.a(current_pc), .b(pc_change), .out(adder_4_out));  // open: cin, cout
  Adder #(.width(32)) adder_5 (.a(current_pc), .b(imm), .out(adder_5_out));  // open: cin, cout
  Multiplexer #(.width(32)) multiplexer_9 (.in0(regfile_1_x_rs2), .in1({32{1'b0}}), .out(multiplexer_9_out), .sel(rst));
  Multiplexer #(.select(4), .width(32)) multiplexer_10 (
    .in10(adder_4_out), .in11(adder_4_out), .in12(pc_change), .out(multiplexer_10_out), .sel(ALU_ctrl));  // open: in0, in1, in2, in3, in4, in5, in6, in7, in8, in9, in13, in14, in15
  Multiplexer #(.width(32)) multiplexer_11 (.in0(regfile_1_x_rs2), .in1(imm), .out(multiplexer_11_out), .sel(op2_src));
  Multiplexer #(.width(32)) multiplexer_12 (
    .in0(pc_change), .in1(multiplexer_10_out), .out(multiplexer_12_out), .sel(control_enable));
  Multiplexer multiplexer_13 (.in0(control_enable), .in1(1'b0), .out(multiplexer_13_out), .sel(rst));
  Multiplexer #(.width(32)) multiplexer_14 (.in0(multiplexer_9_out), .in1({32{1'b0}}), .out(mem_din), .sel(halt));
  Comparator #(.width(32)) comparator_1 (.a(x_rs1), .b({32{1'b0}}), .eq(comparator_1_eq));  // open: gt, lt
  Multiplexer #(.select(4), .width(32)) multiplexer_15 (
    .in0(multiplexer_12_out), .in1(multiplexer_12_out), .in2(multiplexer_12_out), .in3(multiplexer_12_out),
    .in4(multiplexer_12_out), .in5(multiplexer_12_out), .in6(multiplexer_12_out), .in7(multiplexer_12_out),
    .in8(multiplexer_12_out), .in9(multiplexer_12_out), .in10(adder_5_out), .in11(multiplexer_12_out),
    .in12(multiplexer_12_out), .out(multiplexer_15_out), .sel(ALU_ctrl));  // open: in13, in14, in15
  Multiplexer multiplexer_16 (.in0(multiplexer_13_out), .in1(1'b0), .out(control_en), .sel(halt));
  Multiplexer multiplexer_17 (.in0(1'b0), .in1(1'b1), .out(multiplexer_17_out), .sel(comparator_1_eq));
  Multiplexer #(.width(32)) multiplexer_18 (
    .in0(multiplexer_15_out), .in1({32{1'b0}}), .out(multiplexer_18_out), .sel(rst));
  Multiplexer #(.width(32)) multiplexer_19 (.in0(multiplexer_18_out), .in1({32{1'b0}}), .out(control_pc), .sel(halt));
  ALU alu_1 (.x_rs1(x_rs1), .x_rs2_or_imm(multiplexer_11_out), .ALU_ctrl(ALU_ctrl), .ALU_result(pc_change));
  Multiplexer #(.width(32)) multiplexer_20 (
    .in0(multiplexer_32_out), .in1({32{1'b0}}), .out(multiplexer_20_out), .sel(rst));
  Multiplexer #(.select(4)) multiplexer_21 (
    .in0(1'b1), .in1(1'b0), .in2(1'b1), .in3(1'b1), .in4(1'b1), .in5(1'b1), .in6(1'b1), .in7(1'b1),
    .in8(1'b1), .in9(1'b0), .in10(1'b0), .in11(1'b0), .in12(1'b0), .out(reg_en), .sel(ALU_ctrl));  // open: in13, in14, in15
  Multiplexer #(.select(4)) multiplexer_22 (
    .in0(1'b0), .in1(1'b1), .in2(1'b0), .in3(1'b0), .in4(1'b0), .in5(1'b0), .in6(1'b0), .in7(1'b0),
    .in8(1'b0), .in9(1'b1), .in10(1'b0), .in11(1'b0), .in12(1'b0), .out(we), .sel(ALU_ctrl));  // open: in13, in14, in15
  Multiplexer #(.select(4)) multiplexer_23 (
    .in0(1'b0), .in1(1'b0), .in2(1'b0), .in3(1'b0), .in4(1'b0), .in5(1'b0), .in6(1'b0), .in7(1'b0),
    .in8(1'b0), .in9(1'b0), .in10(multiplexer_17_out), .in11(1'b1), .in12(1'b1), .out(control_enable),
    .sel(ALU_ctrl));  // open: in13, in14, in15
  Multiplexer #(.width(32)) multiplexer_24 (.in0(pc_change), .in1({32{1'b0}}), .out(multiplexer_24_out), .sel(rst));
  Multiplexer multiplexer_25 (.in0(we), .in1(1'b0), .out(multiplexer_25_out), .sel(rst));
  Multiplexer multiplexer_26 (.in0(re), .in1(1'b0), .out(multiplexer_26_out), .sel(rst));
  Multiplexer #(.width(32)) multiplexer_27 (.in0(multiplexer_24_out), .in1({32{1'b0}}), .out(alu_result), .sel(halt));
  Multiplexer multiplexer_28 (.in0(multiplexer_26_out), .in1(1'b0), .out(mem_ren), .sel(halt));
  Multiplexer #(.width(32)) multiplexer_29 (.in0(multiplexer_20_out), .in1({32{1'b0}}), .out(wb_data), .sel(halt));
  Multiplexer multiplexer_30 (.in0(multiplexer_25_out), .in1(1'b0), .out(mem_wen), .sel(halt));
  not not_5 (not_5_out, inst[13]);
  not not_6 (not_6_out, inst[14]);
  Multiplexer #(.select(5), .width(4)) multiplexer_31 (
    .in0(4'b0011), .in1(4'b0100), .in2(4'b0000), .in8(4'b1000), .in9(4'b0110), .in13(4'b0111),
    .in18(4'b0101), .in21(4'b1011), .in24(4'b1001), .in25(4'b1010), .in26(4'b0001), .out(multiplexer_31_out),
    .sel({inst[15:13], inst[1:0]}));  // open: in3, in4, in5, in6, in7, in10, in11, in12, in14, in15, in16, in17, in19, in20, in22, in23, in27, in28, in29, in30, in31
  not not_7 (not_7_out, inst[0]);
  not not_8 (not_8_out, inst[13]);
  not not_9 (not_9_out, inst[14]);
  Comparator #(.width(5)) comparator_2 (.a(inst[6:2]), .b({5{1'b0}}), .eq(comparator_2_eq));  // open: gt, lt
  Multiplexer #(.width(32)) multiplexer_32 (.in0(mem_result), .in1(pc_change), .out(multiplexer_32_out), .sel(wb_src));
  Multiplexer #(.width(4)) multiplexer_33 (.in0(4'b0010), .in1(4'b0101), .out(multiplexer_33_out), .sel(inst[12]));
  and and_2 (and_2_out, not_7_out, inst[1], not_8_out, not_9_out, inst[15]);
  nand nand_1 (op2_src, not_5_out, not_6_out, inst[15]);
  Multiplexer #(.width(4)) multiplexer_34 (.in0(multiplexer_31_out), .in1(CR_type), .out(ALU_ctrl), .sel(and_2_out));
  Multiplexer #(.width(4)) multiplexer_35 (
    .in0(multiplexer_33_out), .in1(4'b1100), .out(CR_type), .sel(comparator_2_eq));
  Multiplexer #(.select(4)) multiplexer_36 (
    .in0(1'b0), .in1(1'b0), .in2(1'b0), .in3(1'b0), .in4(1'b0), .in5(1'b0), .in6(1'b0), .in7(1'b0),
    .in8(1'b1), .in9(1'b0), .in10(1'b0), .in11(1'b0), .in12(1'b0), .out(re), .sel(ALU_ctrl));  // open: in13, in14, in15
  Multiplexer #(.select(4)) multiplexer_37 (
    .in0(1'b1), .in1(1'b1), .in2(1'b1), .in3(1'b1), .in4(1'b1), .in5(1'b1), .in6(1'b1), .in7(1'b1),
    .in8(1'b0), .in9(1'b1), .in10(1'b1), .in11(1'b1), .in12(1'b1), .out(wb_src), .sel(ALU_ctrl));  // open: in13, in14, in15

  // Other names for the same wires on the sheet: imm_4_to_0[4:0] = inst[6:2]; offset_2_to_1_B[1:0] = inst[4:3];
  //   offset_3_to_1_J[2:0] = inst[5:3]; rd_s[2:0] = inst[4:2]; rs2_f[4:0] = inst[6:2]; rs2_s[2:0] = inst[4:2];
  //   offset_6 = inst[5]; offset_7_to_6_B[1:0] = inst[6:5]; zimm_3 = inst[5]; offset_5_to_2[3:0] = inst[12:9];
  //   offset_9_to_8_J[1:0] = inst[10:9]; rd_f[4:0] = inst[11:7]; rs1_f[4:0] = inst[11:7]; rs1_s[2:0] = inst[9:7];
  //   zimm_9_to_6[3:0] = inst[10:7]; offset_4_to_3_B[1:0] = inst[11:10]; offset_5_to_3[2:0] = inst[12:10];
  //   offset_4_J = inst[11]; zimm_5_to_4[1:0] = inst[12:11]; offset_5_B = inst[2]; offset_5_J = inst[2];
  //   offset_2 = inst[6]; offset_7_J = inst[6]; zimm_2 = inst[6]; funct4[3:0] = inst[15:12]; imm_5 = inst[12];
  //   offset_8_B = inst[12]; offset_11_J = inst[12]; opcode[1:0] = inst[1:0]; funct3[2:0] = inst[15:13];
  //   offset_6_J = inst[7]; offset_7_to_6[1:0] = inst[8:7]; offset_10_J = inst[8]

  // Notes on the sheet:
  //   Fixed I/O
  //   Don't touch
endmodule

module testbench (
  input  rst,
  output mem_wen,
  output [31:0] mem_din,
  output mem_ren,
  output [31:0] alu_result,
  output control_en,
  output [31:0] control_pc,
  output halt,
  output wb_en,
  output [4:0] wb_addr,
  output [31:0] wb_data
);

  wire clk, inst_en, not_1_out, not_2_out, not_3_out, not_4_out, por_1_out, rst_t;
  wire [15:0] inst, inst_i;
  wire [31:0] current_pc, inst_addr, mem_result;

  not not_1 (not_1_out, inst_i[0]);
  not not_2 (not_2_out, inst_i[1]);
  not not_3 (not_3_out, inst_i[13]);
  not not_4 (not_4_out, inst_i[14]);
  and and_1 (halt, not_1_out, not_2_out, not_3_out, not_4_out, inst_i[15]);
  Clock clock_1 (.out(clk));
  or or_1 (rst_t, rst, por_1_out);
  POR por_1 (.out(por_1_out));
  inst_fetch inst_fetch_1 (
    .clk(clk), .rst(rst_t), .control_en_i(control_en), .control_pc_i(control_pc), .inst_i(inst_i),
    .inst_en_o(inst_en), .current_pc_o(current_pc), .inst_addr_o(inst_addr), .inst_o(inst));
  TOP top_1 (
    .rst(rst_t), .clk(clk), .inst(inst), .mem_result(mem_result), .current_pc(current_pc), .mem_wen(mem_wen),
    .mem_din(mem_din), .mem_ren(mem_ren), .alu_result(alu_result), .control_en(control_en),
    .control_pc(control_pc), .wb_en(wb_en), .wb_addr(wb_addr), .wb_data(wb_data));
  ROM #(.dataWidth(16)) rom_1 (.addr(inst_addr[7:0]), .data(inst_i));
  RAM #(.addrWidth(16), .clearpin("true"), .dataWidth(32), .\type ("nonvolatile")) ram_1 (
    .addr(alu_result[15:0]), .we(mem_wen), .oe(mem_ren), .clk(clk), .din(mem_din), .dout(mem_result),
    .clr(rst_t));

  // Notes on the sheet:
  //   contents of rom_1 (hex, n*v repeats v):
  //   4409 147d c011 bffd 1 1 4111 5429 c422 44b5 48 8482 8526 414c 511 c148 8000 22*0 8000
  //   you can write any instruction in
endmodule

module Regfile (
  input  rst,
  input  clk,
  input  [31:0] x_rd,
  input  wb_en,
  input  [4:0] rs1,
  input  [4:0] rd,
  input  [4:0] rs2,
  output [31:0] x_rs1,
  output [31:0] x_rs2
);

  wire demultiplexer_2_out0, demultiplexer_2_out2, demultiplexer_2_out8, demultiplexer_2_out9,
       demultiplexer_2_out10, demultiplexer_2_out11, demultiplexer_2_out12, demultiplexer_2_out13,
       demultiplexer_2_out14, demultiplexer_2_out15;
  wire [31:0] demultiplexer_1_out0, demultiplexer_1_out2, demultiplexer_1_out8, demultiplexer_1_out9,
       demultiplexer_1_out10, demultiplexer_1_out11, demultiplexer_1_out12, demultiplexer_1_out13,
       demultiplexer_1_out14, demultiplexer_1_out15, register_1_q, x2_q, x8_q, x9_q, x10_q, x11_q, x12_q,
       x13_q, x14_q, x15_q;

  Demultiplexer #(.select(4), .width(32)) demultiplexer_1 (
    .out0(demultiplexer_1_out0), .out2(demultiplexer_1_out2), .out8(demultiplexer_1_out8),
    .out9(demultiplexer_1_out9), .out10(demultiplexer_1_out10), .out11(demultiplexer_1_out11),
    .out12(demultiplexer_1_out12), .out13(demultiplexer_1_out13), .out14(demultiplexer_1_out14),
    .out15(demultiplexer_1_out15), .in(x_rd), .sel(rd[3:0]));  // open: out1, out3, out4, out5, out6, out7
  Demultiplexer #(.select(4)) demultiplexer_2 (
    .out0(demultiplexer_2_out0), .out2(demultiplexer_2_out2), .out8(demultiplexer_2_out8),
    .out9(demultiplexer_2_out9), .out10(demultiplexer_2_out10), .out11(demultiplexer_2_out11),
    .out12(demultiplexer_2_out12), .out13(demultiplexer_2_out13), .out14(demultiplexer_2_out14),
    .out15(demultiplexer_2_out15), .in(wb_en), .sel(rd[3:0]));  // open: out1, out3, out4, out5, out6, out7
  Register #(.width(32)) register_1 (
    .D(demultiplexer_1_out0), .en(demultiplexer_2_out0), .clk(clk), .Q(register_1_q), .clr(rst));
  Register #(.width(32)) x2 (.D(demultiplexer_1_out2), .en(demultiplexer_2_out2), .clk(clk), .Q(x2_q), .clr(rst));
  Register #(.width(32)) x8 (.D(demultiplexer_1_out8), .en(demultiplexer_2_out8), .clk(clk), .Q(x8_q), .clr(rst));
  Register #(.width(32)) x9 (.D(demultiplexer_1_out9), .en(demultiplexer_2_out9), .clk(clk), .Q(x9_q), .clr(rst));
  Register #(.width(32)) x10 (.D(demultiplexer_1_out10), .en(demultiplexer_2_out10), .clk(clk), .Q(x10_q), .clr(rst));
  Register #(.width(32)) x11 (.D(demultiplexer_1_out11), .en(demultiplexer_2_out11), .clk(clk), .Q(x11_q), .clr(rst));
  Register #(.width(32)) x12 (.D(demultiplexer_1_out12), .en(demultiplexer_2_out12), .clk(clk), .Q(x12_q), .clr(rst));
  Register #(.width(32)) x13 (.D(demultiplexer_1_out13), .en(demultiplexer_2_out13), .clk(clk), .Q(x13_q), .clr(rst));
  Register #(.width(32)) x14 (.D(demultiplexer_1_out14), .en(demultiplexer_2_out14), .clk(clk), .Q(x14_q), .clr(rst));
  Register #(.width(32)) x15 (.D(demultiplexer_1_out15), .en(demultiplexer_2_out15), .clk(clk), .Q(x15_q), .clr(rst));
  Multiplexer #(.select(4), .width(32)) multiplexer_1 (
    .in0(register_1_q), .in2(x2_q), .in8(x8_q), .in9(x9_q), .in10(x10_q), .in11(x11_q), .in12(x12_q),
    .in13(x13_q), .in14(x14_q), .in15(x15_q), .out(x_rs1), .sel(rs1[3:0]));  // open: in1, in3, in4, in5, in6, in7
  Multiplexer #(.select(4), .width(32)) multiplexer_2 (
    .in0(register_1_q), .in2(x2_q), .in8(x8_q), .in9(x9_q), .in10(x10_q), .in11(x11_q), .in12(x12_q),
    .in13(x13_q), .in14(x14_q), .in15(x15_q), .out(x_rs2), .sel(rs2[3:0]));  // open: in1, in3, in4, in5, in6, in7
endmodule

module ALU_4bit (
  input  [3:0] A,
  input  [3:0] B,
  input  [3:0] opcode,
  output Z,
  output V,
  output C,
  output N,
  output [3:0] Y
);

  wire [3:0] arithmetic_unit_1_y, logic_unit_1_y, multiplexer_1_out, multiplexer_2_out, not_1_out, not_2_out;

  assign not_1_out = ~A;  // NOT_Gate not_1, 4 bits wide
  assign not_2_out = ~B;  // NOT_Gate not_2, 4 bits wide
  Multiplexer #(.width(4)) multiplexer_1 (.in0(A), .in1(not_1_out), .out(multiplexer_1_out), .sel(opcode[0]));
  Multiplexer #(.width(4)) multiplexer_2 (.in0(B), .in1(not_2_out), .out(multiplexer_2_out), .sel(opcode[1]));
  Arithmetic_Unit arithmetic_unit_1 (
    .cin(opcode[2]), .A(multiplexer_1_out), .B(multiplexer_2_out), .Y(arithmetic_unit_1_y), .overflow(V),
    .cout(C));
  Logic_Unit logic_unit_1 (.A(A), .B(multiplexer_2_out), .f2(opcode[2]), .f0(opcode[0]), .Y(logic_unit_1_y));
  Multiplexer #(.width(4)) multiplexer_3 (
    .in0(arithmetic_unit_1_y), .in1(logic_unit_1_y), .out({N, Y[2:0]}), .sel(opcode[3]));
  nor nor_1 (Z, Y[0], Y[1], Y[2], N);

  assign Y[3] = N;
endmodule

module Arithmetic_Unit (
  input  cin,
  input  [3:0] A,
  input  [3:0] B,
  output [3:0] Y,
  output overflow,
  output cout
);

  wire adder_1_cout, adder_2_cout, adder_3_cout;

  Adder #(.width(1)) adder_1 (.a(A[0]), .b(B[0]), .out(Y[0]), .cin(cin), .cout(adder_1_cout));
  Adder #(.width(1)) adder_2 (.a(A[1]), .b(B[1]), .out(Y[1]), .cin(adder_1_cout), .cout(adder_2_cout));
  Adder #(.width(1)) adder_3 (.a(A[2]), .b(B[2]), .out(Y[2]), .cin(adder_2_cout), .cout(adder_3_cout));
  Adder #(.width(1)) adder_4 (.a(A[3]), .b(B[3]), .out(Y[3]), .cin(adder_3_cout), .cout(cout));
  xor xor_1 (overflow, adder_3_cout, cout);
endmodule

module Logic_Unit (
  input  [3:0] A,
  input  [3:0] B,
  input  f2,
  input  f0,
  output [3:0] Y
);

  wire [3:0] and_1_out, or_1_out, xor_1_out;

  assign and_1_out = A & B;  // AND_Gate and_1, 4 bits wide
  assign or_1_out = A | B;  // OR_Gate or_1, 4 bits wide
  assign xor_1_out = A ^ B;  // XOR_Gate xor_1, 4 bits wide
  Multiplexer #(.select(2), .width(4)) multiplexer_1 (
    .in0(and_1_out), .in1(or_1_out), .in2(xor_1_out), .in3(B), .out(Y), .sel({f2, f0}));
endmodule

module Arithmetic_Unit_32bit (
  input  cin,
  input  [31:0] A,
  input  [31:0] B,
  output [3:0] Y,
  output overflow,
  output cout
);

  wire adder_1_cout, adder_2_cout, adder_3_cout, adder_4_cout;

  Adder #(.width(1)) adder_1 (.cin(cin), .cout(adder_1_cout));  // open: a, b, out
  Adder #(.width(1)) adder_2 (.cin(adder_1_cout), .cout(adder_2_cout));  // open: a, b, out
  Adder #(.width(1)) adder_3 (.cin(adder_2_cout), .cout(adder_3_cout));  // open: a, b, out
  Adder #(.width(1)) adder_4 (.cin(adder_3_cout), .cout(adder_4_cout));  // open: a, b, out
  Adder #(.width(1)) adder_5 (.cin(adder_4_cout));  // open: a, b, out, cout
  // XOR_Gate xor_1 has open pins: out=overflow
  // Pins of 4 and 32 bits meet at B
endmodule

module Logic_Unit_32bit (
  input  [31:0] A,
  input  [31:0] B,
  input  f2,
  input  f0,
  output [31:0] Y
);

  wire [31:0] and_1_out, or_1_out, xor_1_out;

  assign and_1_out = A & B;  // AND_Gate and_1, 32 bits wide
  assign or_1_out = A | B;  // OR_Gate or_1, 32 bits wide
  assign xor_1_out = A ^ B;  // XOR_Gate xor_1, 32 bits wide
  Multiplexer #(.select(2), .width(32)) multiplexer_1 (
    .in0(and_1_out), .in1(or_1_out), .in2(xor_1_out), .in3(B), .out(Y), .sel({f2, f0}));
endmodule

module ALU (
  input  [31:0] x_rs1,
  input  [31:0] x_rs2_or_imm,
  input  [3:0] ALU_ctrl,
  output [31:0] ALU_result
);

  wire [4:0] adder_8_out, not_1_out;
  wire [17:12] shifter_1_out_2;
  wire [31:0] add, addi, addi4spn, beqz, bit_extender_1_out, bit_extender_2_out, bit_extender_3_out,
       bit_extender_4_out, bit_extender_6_out, j, li, lui, lw, mv, shifter_1_out, slli, sw, swsp;

  assign bit_extender_1_out = {{25{1'b0}}, x_rs2_or_imm[6:0]};  // Bit_Extender bit_extender_1
  assign bit_extender_2_out = {{23{1'b0}}, x_rs2_or_imm[8:0]};  // Bit_Extender bit_extender_2
  assign bit_extender_3_out = {{25{1'b0}}, x_rs2_or_imm[6:0]};  // Bit_Extender bit_extender_3
  assign bit_extender_4_out = {{25{1'b0}}, x_rs2_or_imm[6:0]};  // Bit_Extender bit_extender_4
  assign li = {{26{x_rs2_or_imm[5]}}, x_rs2_or_imm[5:0]};  // Bit_Extender bit_extender_5
  Adder #(.width(32)) adder_1 (.a(x_rs1), .b(bit_extender_1_out), .out(swsp));  // open: cin, cout
  assign bit_extender_6_out = {{26{x_rs2_or_imm[5]}}, x_rs2_or_imm[5:0]};  // Bit_Extender bit_extender_6
  Adder #(.width(32)) adder_2 (.a(x_rs1), .b(x_rs2_or_imm), .out(add));  // open: cin, cout
  Shifter #(.width(32)) shifter_1 (
    .in(x_rs2_or_imm), .\dist (5'b01100), .out({shifter_1_out[31:18], shifter_1_out_2, shifter_1_out[11:0]}));
  Adder #(.width(32)) adder_3 (.a(x_rs1), .b(bit_extender_3_out), .out(lw));  // open: cin, cout
  Adder #(.width(32)) adder_4 (.a(x_rs1), .b(bit_extender_4_out), .out(sw));  // open: cin, cout
  assign beqz = {{23{x_rs2_or_imm[8]}}, x_rs2_or_imm[8:0]};  // Bit_Extender bit_extender_7
  assign j = {{20{x_rs2_or_imm[11]}}, x_rs2_or_imm[11:0]};  // Bit_Extender bit_extender_8
  Shifter #(.width(32)) shifter_2 (.in(x_rs1), .\dist (x_rs2_or_imm[4:0]), .out(slli));
  Adder #(.width(32)) adder_5 (.a(x_rs1), .b(bit_extender_2_out), .out(addi4spn));  // open: cin, cout
  Adder #(.width(32)) adder_6 (.a(bit_extender_6_out), .b(x_rs1), .out(addi));  // open: cin, cout
  Adder #(.width(32)) adder_7 (.a({32{1'b0}}), .b(x_rs2_or_imm), .out(mv));  // open: cin, cout
  assign lui = {{14{shifter_1_out_2[17]}}, {shifter_1_out_2, {12{1'b0}}}};  // Bit_Extender bit_extender_9
  // NOT_Gate not_1 has open pins: in=open, out=not_1_out
  Adder #(.width(5)) adder_8 (.a(not_1_out), .b(5'b00001), .out(adder_8_out));  // open: cin, cout
  Multiplexer #(.select(4), .width(32)) multiplexer_1 (
    .in0(slli), .in1(swsp), .in2(mv), .in3(addi4spn), .in4(addi), .in5(add), .in6(li), .in7(lui), .in8(lw),
    .in9(sw), .in10(beqz), .in11(j), .in12(x_rs1), .out(ALU_result), .sel(ALU_ctrl));  // open: in13, in14, in15

  // Other names for the same wires on the sheet: jr[31:0] = x_rs1
endmodule

module control_logic (
  input  [15:0] in_1
);

  wire and_1_out, comparator_1_eq, not_2_out, not_3_out, not_4_out, op2_src, wb_src;
  wire [1:1] not_1_out;
  wire [2:0] ALU_ctrl;
  wire [3:0] CR_type, multiplexer_3_out;

  not not_1 (not_1_out[1], in_1[12]);
  not not_2 (not_2_out, in_1[13]);
  not not_3 (not_3_out, in_1[14]);
  and and_1 (and_1_out, not_2_out, not_3_out);
  Multiplexer multiplexer_1 (.in0(in_1[12]), .in1(and_1_out), .out(wb_src), .sel(op2_src));
  Multiplexer #(.width(3)) multiplexer_2 (
    .in0({in_1[12], not_1_out[1], in_1[12]}), .in1({in_1[0], in_1[14:13]}), .out(ALU_ctrl), .sel(op2_src));
  not not_4 (not_4_out, in_1[15]);
  Multiplexer #(.width(4)) multiplexer_3 (.in0(4'b0010), .in1(4'b0101), .out(multiplexer_3_out), .sel(in_1[12]));
  Comparator #(.width(5)) comparator_1 (.a(in_1[6:2]), .b({5{1'b0}}), .eq(comparator_1_eq));  // open: gt, lt
  or or_1 (op2_src, in_1[14], not_4_out);
  Multiplexer #(.width(4)) multiplexer_4 (.in0(multiplexer_3_out), .in1(4'b1100), .out(CR_type), .sel(comparator_1_eq));

  // Other names for the same wires on the sheet: funct3[2:0] = in_1[15:13]; funct4[3:0] = in_1[15:12];
  //   zimm_5_to_4[1:0] = in_1[13:12]; opcode[1:0] = in_1[1:0]; imm_5 = in_1[12]; offset_5_to_2[3:0] = in_1[12:9];
  //   offset_5_to_3[2:0] = in_1[12:10]; offset_8_B = in_1[12]; offset_11_J = in_1[12]; imm_4_to_0[4:0] = in_1[6:2];
  //   offset_2_to_1_B[1:0] = in_1[4:3]; offset_3_to_1_J[2:0] = in_1[5:3]; rd_s[2:0] = in_1[4:2]; rs2[4:0] = in_1[6:2];
  //   rs2_s[2:0] = in_1[4:2]; offset_6 = in_1[5]; offset_7_to_6_B[1:0] = in_1[6:5]; offset_4_J = in_1[11];
  //   offset_4_to_3_B[1:0] = in_1[11:10]; rd[4:0] = in_1[11:7]; zimm_9_to_6[3:0] = in_1[11:8]; offset_2 = in_1[6];
  //   offset_7_J = in_1[6]; zimm_3 = in_1[6]; offset_9_to_8_J[1:0] = in_1[10:9]; rs1_s[2:0] = in_1[9:7];
  //   offset_6_J = in_1[7]; offset_7_to_6[1:0] = in_1[8:7]; zimm_2 = in_1[7]; offset_10_J = in_1[8];
  //   offset_5_B = in_1[2]; offset_5_J = in_1[2]
endmodule

module controller (
  input  [15:0] in_1
);

  wire and_1_out, comparator_1_eq, control_en, mem_ren, mem_wen, not_1_out, not_2_out, not_3_out, not_4_out,
       op2_src, undriven, wb_en, wb_src;
  wire [3:0] ALU_ctrl, CR_type, multiplexer_6_out, multiplexer_7_out;

  Multiplexer #(.select(4)) multiplexer_1 (
    .in0(1'b0), .in1(1'b1), .in2(1'b0), .in3(1'b0), .in4(1'b0), .in5(1'b0), .in6(1'b0), .in7(1'b0),
    .in8(1'b0), .in9(1'b1), .in10(1'b0), .in11(1'b0), .in12(1'b0), .out(mem_wen), .sel(ALU_ctrl));  // open: in13, in14, in15
  Multiplexer #(.select(4)) multiplexer_2 (
    .in0(1'b0), .in1(1'b0), .in2(1'b0), .in3(1'b0), .in4(1'b0), .in5(1'b0), .in6(1'b0), .in7(1'b0),
    .in8(1'b1), .in9(1'b0), .in10(1'b0), .in11(1'b0), .in12(1'b0), .out(wb_src), .sel(ALU_ctrl));  // open: in13, in14, in15
  Multiplexer #(.select(4)) multiplexer_3 (
    .in0(1'b0), .in1(1'b0), .in2(1'b0), .in3(1'b0), .in4(1'b0), .in5(1'b0), .in6(1'b0), .in7(1'b0),
    .in8(1'b0), .in9(1'b0), .in10(undriven), .in11(1'b1), .in12(1'b1), .out(control_en), .sel(ALU_ctrl));  // open: in13, in14, in15
  Multiplexer #(.select(4)) multiplexer_4 (
    .in0(1'b1), .in1(1'b0), .in2(1'b1), .in3(1'b1), .in4(1'b1), .in5(1'b1), .in6(1'b1), .in7(1'b1),
    .in8(1'b0), .in9(1'b0), .in10(1'b0), .in11(1'b0), .in12(1'b0), .out(wb_en), .sel(ALU_ctrl));  // open: in13, in14, in15
  Multiplexer #(.select(4)) multiplexer_5 (
    .in0(1'b0), .in1(1'b0), .in2(1'b0), .in3(1'b0), .in4(1'b0), .in5(1'b0), .in6(1'b0), .in7(1'b0),
    .in8(1'b1), .in9(1'b0), .in10(1'b0), .in11(1'b0), .in12(1'b0), .out(mem_ren), .sel(ALU_ctrl));  // open: in13, in14, in15
  not not_1 (not_1_out, in_1[0]);
  not not_2 (not_2_out, in_1[15]);
  Multiplexer #(.select(5), .width(4)) multiplexer_6 (
    .in0(4'b0011), .in1(4'b0100), .in2(4'b0000), .in8(4'b1000), .in9(4'b0110), .in13(4'b0111),
    .in18(4'b0101), .in21(4'b1011), .in24(4'b1001), .in25(4'b1010), .in26(4'b0001), .out(multiplexer_6_out),
    .sel({in_1[15:13], in_1[1:0]}));  // open: in3, in4, in5, in6, in7, in10, in11, in12, in14, in15, in16, in17, in19, in20, in22, in23, in27, in28, in29, in30, in31
  not not_3 (not_3_out, in_1[13]);
  not not_4 (not_4_out, in_1[14]);
  Comparator #(.width(5)) comparator_1 (.a(in_1[6:2]), .b({5{1'b0}}), .eq(comparator_1_eq));  // open: gt, lt
  or or_1 (op2_src, in_1[14], not_2_out);
  Multiplexer #(.width(4)) multiplexer_7 (.in0(4'b0010), .in1(4'b0101), .out(multiplexer_7_out), .sel(in_1[12]));
  and and_1 (and_1_out, not_1_out, in_1[1], not_3_out, not_4_out, in_1[15]);
  Multiplexer #(.width(4)) multiplexer_8 (.in0(multiplexer_6_out), .in1(CR_type), .out(ALU_ctrl), .sel(and_1_out));
  Multiplexer #(.width(4)) multiplexer_9 (.in0(multiplexer_7_out), .in1(4'b1100), .out(CR_type), .sel(comparator_1_eq));

  // Other names for the same wires on the sheet: opcode[1:0] = in_1[1:0]; funct3[2:0] = in_1[15:13];
  //   funct4[3:0] = in_1[15:12]; zimm_5_to_4[1:0] = in_1[13:12]; imm_4_to_0[4:0] = in_1[6:2];
  //   offset_2_to_1_B[1:0] = in_1[4:3]; offset_3_to_1_J[2:0] = in_1[5:3]; rd_s[2:0] = in_1[4:2]; rs2[4:0] = in_1[6:2];
  //   rs2_s[2:0] = in_1[4:2]; offset_6 = in_1[5]; offset_7_to_6_B[1:0] = in_1[6:5]; offset_4_J = in_1[11];
  //   offset_4_to_3_B[1:0] = in_1[11:10]; offset_5_to_2[3:0] = in_1[12:9]; offset_5_to_3[2:0] = in_1[12:10];
  //   rd[4:0] = in_1[11:7]; zimm_9_to_6[3:0] = in_1[11:8]; imm_5 = in_1[12]; offset_8_B = in_1[12];
  //   offset_11_J = in_1[12]; offset_2 = in_1[6]; offset_7_J = in_1[6]; zimm_3 = in_1[6];
  //   offset_9_to_8_J[1:0] = in_1[10:9]; rs1_s[2:0] = in_1[9:7]; offset_6_J = in_1[7]; offset_7_to_6[1:0] = in_1[8:7];
  //   zimm_2 = in_1[7]; offset_10_J = in_1[8]; offset_5_B = in_1[2]; offset_5_J = in_1[2]
endmodule
